// Logisim project processor.circ as structural Verilog: 10 circuits, main circuit main
module main (
  output [4:0] out_1,
  output [31:0] out_2,
  output [31:0] ALU_Result,
  output [31:0] Next_Address,
  output [5:0] out_5,
  output [5:0] out_6,
  output [4:0] out_7,
  output [15:0] out_8,
  output [4:0] out_9,
  output [31:0] DM_output,
  output [31:0] Write_Data__Data_Memory_input,
  output [31:0] Write_Data__Register_input,
  output [4:0] out_13,
  output [3:0] ALU_control,
  output [31:0] out_15,
  output [31:0] ALU_mux_0,
  output [31:0] AMU_mux_1,
  output [31:0] out_18
);

  wire alu_1_zeroflag, and_1_out, clk, Control_Unit_alusrc, Control_Unit_branch, Control_Unit_jump,
       Control_Unit_memread, Control_Unit_memtoreg, Control_Unit_memwrite, Control_Unit_regdst,
       Control_Unit_regwrite;
  wire [1:0] Control_Unit_aluop;
  wire [4:0] multiplexer_1_out;
  wire [31:0] adder_1_out, adder_2_out, multiplexer_3_out, pc_1_current_address, shiftleft_1_shifted,
       shiftleftappend_1_next_address;

  Clock clock_1 (.out(clk));
  IM im_1 (.Instruction({out_2[31:11], out_1, out_2[5:0]}), .Address(pc_1_current_address), .clk(clk));
  PC pc_1 (.Clock(clk), .Next_address(Next_Address), .Current_Address(pc_1_current_address));
  Adder #(.width(32)) adder_1 (.a(pc_1_current_address), .b(32'h4), .out(adder_1_out));  // open: cin, cout
  ShiftLeftAppend shiftleftappend_1 (
    .PC_4(adder_1_out), .Instruction({out_2[31:11], out_1, out_2[5:0]}),
    .Next_Address(shiftleftappend_1_next_address));
  ControlUnit Control_Unit (
    .OPCode(out_2[31:26]), .RegDst(Control_Unit_regdst), .AluSrc(Control_Unit_alusrc),
    .MemToReg(Control_Unit_memtoreg), .RegWrite(Control_Unit_regwrite), .Jump(Control_Unit_jump),
    .MemRead(Control_Unit_memread), .MemWrite(Control_Unit_memwrite), .Branch(Control_Unit_branch),
    .ALUOp(Control_Unit_aluop));
  Multiplexer #(.width(5), .enable("false")) multiplexer_1 (
    .in0(out_2[20:16]), .in1(out_2[15:11]), .out(multiplexer_1_out), .sel(Control_Unit_regdst));
  assign AMU_mux_1 = {{16{out_2[15]}}, {out_2[15:11], out_1, out_2[5:0]}};  // Bit_Extender bit_extender_1
  RegFile regfile_1 (
    .RegWrite(Control_Unit_regwrite), .Read_reg_1(out_2[25:21]), .Read_reg_2(out_2[20:16]),
    .WriteReg(multiplexer_1_out), .WriteData(Write_Data__Register_input), .Read_data_1(out_15),
    .Read_data_2(ALU_mux_0), .Clock(clk));
  ShiftLeft shiftleft_1 (.in(AMU_mux_1), .Shifted(shiftleft_1_shifted));
  Multiplexer #(.width(32), .enable("false")) multiplexer_2 (
    .in0(ALU_mux_0), .in1(AMU_mux_1), .out(out_18), .sel(Control_Unit_alusrc));
  ALU_control alu_control_1 (.ALUOp(Control_Unit_aluop), .ALU_Control(ALU_control), .Funct_ALU(out_2[5:0]));
  Adder #(.width(32)) adder_2 (.a(adder_1_out), .b(shiftleft_1_shifted), .out(adder_2_out));  // open: cin, cout
  ALU alu_1 (
    .ALU_in_1(out_15), .ALU_in_2(out_18), .ZeroFlag(alu_1_zeroflag), .ALU_Out(ALU_Result),
    .ALU_ControlBits(ALU_control));
  and and_1 (and_1_out, Control_Unit_branch, alu_1_zeroflag);
  DM dm_1 (
    .Address(ALU_Result), .ReadData(DM_output), .MemWrite(Control_Unit_memwrite), .WriteData(ALU_mux_0),
    .MemRead(Control_Unit_memread), .clk(clk));
  Multiplexer #(.width(32), .enable("false")) multiplexer_3 (
    .in0(adder_1_out), .in1(adder_2_out), .out(multiplexer_3_out), .sel(and_1_out));
  Multiplexer #(.width(32), .enable("false")) multiplexer_4 (
    .in0(ALU_Result), .in1(DM_output), .out(Write_Data__Register_input), .sel(Control_Unit_memtoreg));
  Multiplexer #(.width(32), .enable("false")) multiplexer_5 (
    .in0(multiplexer_3_out), .in1(shiftleftappend_1_next_address), .out(Next_Address), .sel(Control_Unit_jump));

  assign out_2[10:6] = out_1;
  assign out_5 = out_2[31:26];
  assign out_6 = out_2[5:0];
  assign out_7 = out_2[25:21];
  assign out_8 = {out_2[15:11], out_1, out_2[5:0]};
  assign out_9 = out_2[20:16];
  assign out_13 = out_2[15:11];
  assign Write_Data__Data_Memory_input = ALU_mux_0;

  // Other names for the same wires on the sheet: AC[3:0] = ALU_control;
  //   address[15:0] = {out_2[15:11], out_1, out_2[5:0]}; funct[5:0] = out_2[5:0];
  //   ins[31:0] = {out_2[31:11], out_1, out_2[5:0]}; shamt[4:0] = out_1; rd[4:0] = out_2[15:11];
  //   ALUin2[31:0] = out_18; dmout[31:0] = DM_output; rt[4:0] = out_2[20:16]; rs[4:0] = out_2[25:21];
  //   opcode[5:0] = out_2[31:26]; NA[31:0] = Next_Address; RD1[31:0] = out_15; Res[31:0] = ALU_Result;
  //   sgn[31:0] = AMU_mux_1; RD2[31:0] = ALU_mux_0; WD_DM[31:0] = ALU_mux_0;
  //   WD_reg[31:0] = Write_Data__Register_input

  // Notes on the sheet:
  //   Added all these tunnels for debugging
  //   Instruction [31-26]
  //   instruction[15-0]
  //   RegDst
  //   instruction[5-0]
  //   Combined MIPS Processor Circuit
  //   ALUSrc
  //   ALUOp
  //   B23CS1040
endmodule

// ALU_ctrl
module ALU_control (
  input  [1:0] ALUOp,
  input  [5:0] Funct_ALU,
  output [3:0] ALU_Control
);

  wire and_1_out, and_2_out, and_3_out, not_1_out, not_2_out, not_3_out;

  not not_1 (not_1_out, Funct_ALU[1]);
  and and_1 (and_1_out, ALUOp[1], Funct_ALU[1]);
  not not_2 (not_2_out, ALUOp[1]);
  not not_3 (not_3_out, Funct_ALU[2]);
  and and_2 (and_2_out, ALUOp[1], Funct_ALU[0]);
  and and_3 (and_3_out, ALUOp[1], Funct_ALU[3]);
  and and_4 (ALU_Control[3], ALUOp[1], Funct_ALU[3], not_1_out);
  or or_1 (ALU_Control[2], ALUOp[0], and_1_out);
  or or_2 (ALU_Control[1], not_2_out, not_3_out);
  or or_3 (ALU_Control[0], and_2_out, and_3_out);

  // Notes on the sheet:
  //   F5
  //   AluOp1
  //   ALUOp0
  //   Don't care
  //   F4
  //   Don't care
  //   F3
  //   F2
  //   F1
  //   F0
  //   ALU Control
  //   Based on fig 4.13 from book
  //   ALU_in_3
  //   ALU_in_2
  //   ALU_in_1
  //   ALU_in_0
endmodule

module ALU (
  input  [31:0] ALU_in_1,
  input  [31:0] ALU_in_2,
  input  [3:0] ALU_ControlBits,
  output ZeroFlag,
  output [31:0] ALU_Out
);

  wire Add_out, comparator_1_lt, Sub_out;
  wire [31:0] adder_1_out, AND_out, bit_extender_1_out, NOR_out, OR_out, subtractor_1_out;

  assign AND_out = ALU_in_1 & ALU_in_2;  // AND_Gate AND, 32 bits wide
  assign OR_out = ALU_in_1 | ALU_in_2;  // OR_Gate OR, 32 bits wide
  Adder #(.width(32)) adder_1 (.a(ALU_in_1), .b(ALU_in_2), .out(adder_1_out), .cout(Add_out));  // open: cin
  Subtractor #(.width(32)) subtractor_1 (
    .a(ALU_in_1), .b(ALU_in_2), .out(subtractor_1_out), .bout(Sub_out));  // open: bin
  Comparator #(.width(32)) comparator_1 (.a(ALU_in_1), .b(ALU_in_2), .lt(comparator_1_lt));  // open: gt, eq
  assign bit_extender_1_out = {{31{1'b0}}, comparator_1_lt};  // Bit_Extender bit_extender_1
  assign NOR_out = ~(ALU_in_1 | ALU_in_2);  // NOR_Gate NOR, 32 bits wide
  Multiplexer #(.select(4), .width(32)) multiplexer_1 (
    .in0(AND_out), .in1(OR_out), .in2(adder_1_out), .in6(subtractor_1_out), .in7(bit_extender_1_out),
    .in12(NOR_out), .out(ALU_Out), .sel(ALU_ControlBits));  // open: in3, in4, in5, in8, in9, in10, in11, in13, in14, in15, en
  Comparator #(.width(32)) comparator_2 (.a({32{1'b0}}), .b(ALU_Out), .eq(ZeroFlag));  // open: gt, lt

  // Notes on the sheet:
  //   ALU - Arithmetic Logic Unit
endmodule

module RegFile (
  input  RegWrite,
  input  [4:0] Read_reg_1,
  input  [4:0] Read_reg_2,
  input  [4:0] WriteReg,
  input  [31:0] WriteData,
  input  Clock,
  output [31:0] Read_data_1,
  output [31:0] Read_data_2
);

  wire demultiplexer_1_out0, demultiplexer_1_out1, demultiplexer_1_out2, demultiplexer_1_out3,
       demultiplexer_1_out4, demultiplexer_1_out5, demultiplexer_1_out6, demultiplexer_1_out7,
       demultiplexer_1_out8, demultiplexer_1_out9, demultiplexer_1_out10, demultiplexer_1_out11,
       demultiplexer_1_out12, demultiplexer_1_out13, demultiplexer_1_out14, demultiplexer_1_out15,
       demultiplexer_1_out16, demultiplexer_1_out17, demultiplexer_1_out18, demultiplexer_1_out19,
       demultiplexer_1_out20, demultiplexer_1_out21, demultiplexer_1_out22, demultiplexer_1_out23,
       demultiplexer_1_out24, demultiplexer_1_out25, demultiplexer_1_out26, demultiplexer_1_out27,
       demultiplexer_1_out28, demultiplexer_1_out29, demultiplexer_1_out30, demultiplexer_1_out31;
  wire [31:0] register_1_q, register_2_q, register_3_q, register_4_q, register_5_q, register_6_q,
       register_7_q, register_8_q, register_9_q, register_10_q, register_11_q, register_12_q, register_13_q,
       register_14_q, register_15_q, register_16_q, register_17_q, register_18_q, register_19_q,
       register_20_q, register_21_q, register_22_q, register_23_q, register_24_q, register_25_q,
       register_26_q, register_27_q, register_28_q, register_29_q, register_30_q, register_31_q,
       register_32_q;

  Demultiplexer #(.select(5)) demultiplexer_1 (
    .out0(demultiplexer_1_out0), .out1(demultiplexer_1_out1), .out2(demultiplexer_1_out2),
    .out3(demultiplexer_1_out3), .out4(demultiplexer_1_out4), .out5(demultiplexer_1_out5),
    .out6(demultiplexer_1_out6), .out7(demultiplexer_1_out7), .out8(demultiplexer_1_out8),
    .out9(demultiplexer_1_out9), .out10(demultiplexer_1_out10), .out11(demultiplexer_1_out11),
    .out12(demultiplexer_1_out12), .out13(demultiplexer_1_out13), .out14(demultiplexer_1_out14),
    .out15(demultiplexer_1_out15), .out16(demultiplexer_1_out16), .out17(demultiplexer_1_out17),
    .out18(demultiplexer_1_out18), .out19(demultiplexer_1_out19), .out20(demultiplexer_1_out20),
    .out21(demultiplexer_1_out21), .out22(demultiplexer_1_out22), .out23(demultiplexer_1_out23),
    .out24(demultiplexer_1_out24), .out25(demultiplexer_1_out25), .out26(demultiplexer_1_out26),
    .out27(demultiplexer_1_out27), .out28(demultiplexer_1_out28), .out29(demultiplexer_1_out29),
    .out30(demultiplexer_1_out30), .out31(demultiplexer_1_out31), .in(RegWrite), .sel(WriteReg));  // open: en
  Register #(.width(32)) register_1 (
    .D(WriteData), .en(demultiplexer_1_out1), .Q(register_1_q), .clk(Clock));  // open: clr
  Register #(.width(32)) register_2 (
    .D(WriteData), .en(demultiplexer_1_out3), .Q(register_2_q), .clk(Clock));  // open: clr
  Register #(.width(32)) register_3 (
    .D(WriteData), .en(demultiplexer_1_out5), .Q(register_3_q), .clk(Clock));  // open: clr
  Register #(.width(32)) register_4 (
    .D(WriteData), .en(demultiplexer_1_out7), .Q(register_4_q), .clk(Clock));  // open: clr
  Register #(.width(32)) register_5 (
    .D(WriteData), .en(demultiplexer_1_out9), .Q(register_5_q), .clk(Clock));  // open: clr
  Register #(.width(32)) register_6 (
    .D(WriteData), .en(demultiplexer_1_out11), .Q(register_6_q), .clk(Clock));  // open: clr
  Register #(.width(32)) register_7 (
    .D(WriteData), .en(demultiplexer_1_out13), .Q(register_7_q), .clk(Clock));  // open: clr
  Register #(.width(32)) register_8 (
    .D(WriteData), .en(demultiplexer_1_out15), .Q(register_8_q), .clk(Clock));  // open: clr
  Register #(.width(32)) register_9 (
    .D(WriteData), .en(demultiplexer_1_out17), .Q(register_9_q), .clk(Clock));  // open: clr
  Register #(.width(32)) register_10 (
    .D(WriteData), .en(demultiplexer_1_out19), .Q(register_10_q), .clk(Clock));  // open: clr
  Register #(.width(32)) register_11 (
    .D(WriteData), .en(demultiplexer_1_out21), .Q(register_11_q), .clk(Clock));  // open: clr
  Register #(.width(32)) register_12 (
    .D(WriteData), .en(demultiplexer_1_out23), .Q(register_12_q), .clk(Clock));  // open: clr
  Register #(.width(32)) register_13 (
    .D(WriteData), .en(demultiplexer_1_out25), .Q(register_13_q), .clk(Clock));  // open: clr
  Register #(.width(32)) register_14 (
    .D(WriteData), .en(demultiplexer_1_out27), .Q(register_14_q), .clk(Clock));  // open: clr
  Register #(.width(32)) register_15 (
    .D(WriteData), .en(demultiplexer_1_out29), .Q(register_15_q), .clk(Clock));  // open: clr
  Register #(.width(32)) register_16 (
    .D(WriteData), .en(demultiplexer_1_out31), .Q(register_16_q), .clk(Clock));  // open: clr
  Register #(.width(32)) register_17 (
    .D(WriteData), .en(demultiplexer_1_out0), .Q(register_17_q), .clk(Clock), .clr(1'b1));
  Register #(.width(32)) register_18 (
    .D(WriteData), .en(demultiplexer_1_out2), .Q(register_18_q), .clk(Clock));  // open: clr
  Register #(.width(32)) register_19 (
    .D(WriteData), .en(demultiplexer_1_out4), .Q(register_19_q), .clk(Clock));  // open: clr
  Register #(.width(32)) register_20 (
    .D(WriteData), .en(demultiplexer_1_out6), .Q(register_20_q), .clk(Clock));  // open: clr
  Register #(.width(32)) register_21 (
    .D(WriteData), .en(demultiplexer_1_out8), .Q(register_21_q), .clk(Clock));  // open: clr
  Register #(.width(32)) register_22 (
    .D(WriteData), .en(demultiplexer_1_out10), .Q(register_22_q), .clk(Clock));  // open: clr
  Register #(.width(32)) register_23 (
    .D(WriteData), .en(demultiplexer_1_out12), .Q(register_23_q), .clk(Clock));  // open: clr
  Register #(.width(32)) register_24 (
    .D(WriteData), .en(demultiplexer_1_out14), .Q(register_24_q), .clk(Clock));  // open: clr
  Register #(.width(32)) register_25 (
    .D(WriteData), .en(demultiplexer_1_out16), .Q(register_25_q), .clk(Clock));  // open: clr
  Register #(.width(32)) register_26 (
    .D(WriteData), .en(demultiplexer_1_out18), .Q(register_26_q), .clk(Clock));  // open: clr
  Register #(.width(32)) register_27 (
    .D(WriteData), .en(demultiplexer_1_out20), .Q(register_27_q), .clk(Clock));  // open: clr
  Register #(.width(32)) register_28 (
    .D(WriteData), .en(demultiplexer_1_out22), .Q(register_28_q), .clk(Clock));  // open: clr
  Register #(.width(32)) register_29 (
    .D(WriteData), .en(demultiplexer_1_out24), .Q(register_29_q), .clk(Clock));  // open: clr
  Register #(.width(32)) register_30 (
    .D(WriteData), .en(demultiplexer_1_out26), .Q(register_30_q), .clk(Clock));  // open: clr
  Register #(.width(32)) register_31 (
    .D(WriteData), .en(demultiplexer_1_out28), .Q(register_31_q), .clk(Clock));  // open: clr
  Register #(.width(32)) register_32 (
    .D(WriteData), .en(demultiplexer_1_out30), .Q(register_32_q), .clk(Clock));  // open: clr
  Multiplexer #(.select(5), .width(32)) multiplexer_1 (
    .in0(register_17_q), .in1(register_1_q), .in2(register_18_q), .in3(register_2_q), .in4(register_19_q),
    .in5(register_3_q), .in6(register_20_q), .in7(register_4_q), .in8(register_21_q), .in9(register_5_q),
    .in10(register_22_q), .in11(register_6_q), .in12(register_23_q), .in13(register_7_q),
    .in14(register_24_q), .in15(register_8_q), .in16(register_25_q), .in17(register_9_q),
    .in18(register_26_q), .in19(register_10_q), .in20(register_27_q), .in21(register_11_q),
    .in22(register_28_q), .in23(register_12_q), .in24(register_29_q), .in25(register_13_q),
    .in26(register_30_q), .in27(register_14_q), .in28(register_31_q), .in29(register_15_q),
    .in30(register_32_q), .in31(register_16_q), .out(Read_data_1), .sel(Read_reg_1));  // open: en
  Multiplexer #(.select(5), .width(32)) multiplexer_2 (
    .in0(register_17_q), .in1(register_1_q), .in2(register_18_q), .in3(register_2_q), .in4(register_19_q),
    .in5(register_3_q), .in6(register_20_q), .in7(register_4_q), .in8(register_21_q), .in9(register_5_q),
    .in10(register_22_q), .in11(register_6_q), .in12(register_23_q), .in13(register_7_q),
    .in14(register_24_q), .in15(register_8_q), .in16(register_25_q), .in17(register_9_q),
    .in18(register_26_q), .in19(register_10_q), .in20(register_27_q), .in21(register_11_q),
    .in22(register_28_q), .in23(register_12_q), .in24(register_29_q), .in25(register_13_q),
    .in26(register_30_q), .in27(register_14_q), .in28(register_31_q), .in29(register_15_q),
    .in30(register_32_q), .in31(register_16_q), .out(Read_data_2), .sel(Read_reg_2));  // open: en

  // Notes on the sheet:
  //   Register File
  //   9
endmodule

module ControlUnit (
  input  [5:0] OPCode,
  output RegDst,
  output AluSrc,
  output MemToReg,
  output RegWrite,
  output Jump,
  output MemRead,
  output MemWrite,
  output Branch,
  output [1:0] ALUOp
);

  wire nor_5_out, nor_6_out, or_1_out;

  nor nor_1 (ALUOp[1], OPCode[0], OPCode[1], OPCode[2], OPCode[3], OPCode[4], OPCode[5]);
  nor nor_2 (ALUOp[0], OPCode[0], OPCode[1], ~OPCode[2], OPCode[3], OPCode[4], OPCode[5]);  // NOR_Gate
  nor nor_3 (MemRead, ~OPCode[0], ~OPCode[1], OPCode[2], OPCode[3], OPCode[4], ~OPCode[5]);  // NOR_Gate
  nor nor_4 (MemWrite, ~OPCode[0], ~OPCode[1], OPCode[2], ~OPCode[3], OPCode[4], ~OPCode[5]);  // NOR_Gate
  nor nor_5 (nor_5_out, OPCode[0], OPCode[1], OPCode[2], ~OPCode[3], OPCode[4], OPCode[5]);  // NOR_Gate
  nor nor_6 (nor_6_out, OPCode[0], ~OPCode[1], OPCode[2], ~OPCode[3], OPCode[4], OPCode[5]);  // NOR_Gate
  nor nor_7 (Jump, OPCode[0], ~OPCode[1], OPCode[2], OPCode[3], OPCode[4], OPCode[5]);  // NOR_Gate
  or or_1 (or_1_out, nor_5_out, nor_6_out);
  or or_2 (RegWrite, ALUOp[1], or_1_out, MemRead);
  or or_3 (AluSrc, MemRead, MemWrite, or_1_out);

  assign Branch = ALUOp[0];
  assign MemToReg = MemRead;
  assign RegDst = ALUOp[1];

  // Notes on the sheet:
  //   Control Unit
endmodule

module IM (
  input  [31:0] Address,
  input  clk,
  output [31:0] Instruction
);

  RAM #(.addrWidth(24), .dataWidth(32)) ram_1 (
    .addr(Address[23:0]), .data(Instruction), .sel(1'b1), .clk(clk), .ld(1'b1), .clr(1'b0));

  // Notes on the sheet:
  //   Instruction Memory
  //   B23CS1040
endmodule

module DM (
  input  [31:0] Address,
  input  MemWrite,
  input  [31:0] WriteData,
  input  MemRead,
  input  clk,
  output [31:0] ReadData
);

  RAM #(.addrWidth(24), .dataWidth(32), .bus("separate")) ram_1 (
    .addr(Address[23:0]), .din(WriteData), .data(ReadData), .str(MemWrite), .sel(1'b1), .clk(clk),
    .ld(MemRead), .clr(1'b0));

  // Notes on the sheet:
  //   Inputs
  //   24 bits from 32-bit Address
  //   Load and Store both options are here for Data Memory
  //   Data Memory
  //   Output
endmodule

module PC (
  input  Clock,
  input  [31:0] Next_address,
  output [31:0] Current_Address
);

  Register #(.width(32)) _32_bit_register (.D(Next_address), .en(1'b1), .Q(Current_Address), .clk(Clock));  // open: clr

  // Other names for the same wires on the sheet: clk = Clock

  // Notes on the sheet:
  //   Address being loaded for instruction
  //   that will be executed in next clock cycle.
  //   Program Counter
endmodule

module ShiftLeft (
  input  [31:0] in,
  output [31:0] Shifted
);

  Shifter #(.width(32)) shifter_1 (.in(in), .\dist (5'b00010), .out(Shifted));

  // Notes on the sheet:
  //   Shift Left
endmodule

module ShiftLeftAppend (
  input  [31:0] Instruction,
  input  [31:0] PC_4,
  output [31:0] Next_Address
);


  assign Next_Address = {PC_4[31:28], Instruction[25:0], 2'b00};

  // Other names for the same wires on the sheet: ins[31:0] = Instruction; ins_25_0[25:0] = Instruction[25:0];
  //   JumpAddress[31:2] = {PC_4[31:28], Instruction[25:0]}

  // Notes on the sheet:
  //   Input
  //   Shift Left 2 and Append PC+4
  //   28 bit output
  //   Output
  //   This circuit component takes in the full 32 bit instruction, gets Instruction [25-0] (26 bit input) to shift left 2 and then appends it with PC+4[28-31]
endmodule
