// Logisim project without_memory.circ as structural Verilog: 5 circuits, main circuit main
module main (
  input  [4:0] in_1,
  input  [31:0] ReadData
);

  wire alu_1_zeroflag, and_1_out, clock_1_out, controlunit_1_alusrc, controlunit_1_branch,
       controlunit_1_memtoreg, controlunit_1_regdst, controlunit_1_regwrite;
  wire [1:0] controlunit_1_aluop;
  wire [3:0] ALU_ctrl_alu_control;
  wire [4:0] multiplexer_1_out;
  wire [31:0] adder_1_out, alu_1_alu_out, bit_extender_1_out, im0_q, multiplexer_2_out, multiplexer_3_out,
       multiplexer_4_out, regfile_1_read_data_1, regfile_1_read_data_2, shifter_1_out;

  Clock clock_1 (.out(clock_1_out));
  Multiplexer #(.width(5), .enable("false")) multiplexer_1 (
    .in0({5{1'b0}}), .in1({5{1'b0}}), .out(multiplexer_1_out), .sel(controlunit_1_regdst));
  ControlUnit controlunit_1 (
    .OPCode({6{1'b0}}), .RegDst(controlunit_1_regdst), .AluSrc(controlunit_1_alusrc),
    .MemToReg(controlunit_1_memtoreg), .RegWrite(controlunit_1_regwrite), .Branch(controlunit_1_branch),
    .ALUOp(controlunit_1_aluop));  // open: Jump, MemRead, MemWrite
  RegFile regfile_1 (
    .RegWrite(controlunit_1_regwrite), .Read_reg_1({5{1'b0}}), .Read_reg_2({5{1'b0}}),
    .WriteReg(multiplexer_1_out), .WriteData(multiplexer_4_out), .Clock(clock_1_out),
    .Read_data_1(regfile_1_read_data_1), .Read_data_2(regfile_1_read_data_2));
  assign bit_extender_1_out = {{16{1'b0}}, {16{1'b0}}};  // Bit_Extender bit_extender_1
  Shifter #(.width(32)) shifter_1 (.in(bit_extender_1_out), .\dist (in_1), .out(shifter_1_out));
  Multiplexer #(.width(32), .enable("false")) multiplexer_2 (
    .in0(regfile_1_read_data_2), .in1(bit_extender_1_out), .out(multiplexer_2_out), .sel(controlunit_1_alusrc));
  ALU_control ALU_ctrl (.ALUOp(controlunit_1_aluop), .Funct_ALU({6{1'b0}}), .ALU_Control(ALU_ctrl_alu_control));
  Adder #(.width(32)) adder_1 (.a(32'h4), .b(shifter_1_out), .out(adder_1_out));  // open: cin, cout
  ALU alu_1 (
    .ALUIn_1(regfile_1_read_data_1), .ALUIn_2(multiplexer_2_out), .ALU_ControlBits(ALU_ctrl_alu_control),
    .ZeroFlag(alu_1_zeroflag), .ALU_Out(alu_1_alu_out));
  and and_1 (and_1_out, controlunit_1_branch, alu_1_zeroflag);
  Multiplexer #(.width(32), .enable("false")) multiplexer_3 (
    .in0(im0_q), .in1(adder_1_out), .out(multiplexer_3_out), .sel(and_1_out));
  Multiplexer #(.width(32), .enable("false")) multiplexer_4 (
    .in0(alu_1_alu_out), .in1(ReadData), .out(multiplexer_4_out), .sel(controlunit_1_memtoreg));
  Register #(.width(32)) im0 (.D(multiplexer_3_out), .en(and_1_out), .Q(im0_q), .clk(clock_1_out));  // open: clr

  // Notes on the sheet:
  //   Instruction [31-26]
  //   Combined MIPS Processor Circuit
  //   instruction[15-0]
  //   RegDst
  //   instruction[5-0]
  //   ALUSrc
  //   ALUOp
endmodule

module ALU_control (
  input  [1:0] ALUOp,
  input  [5:0] Funct_ALU,
  output [3:0] ALU_Control
);

  wire and_1_out, and_2_out, and_3_out, not_1_out, not_2_out, not_3_out;

  not not_1 (not_1_out, Funct_ALU[1]);
  and and_1 (and_1_out, ALUOp[1], Funct_ALU[1]);
  not not_2 (not_2_out, ALUOp[1]);
  not not_3 (not_3_out, Funct_ALU[2]);
  and and_2 (and_2_out, ALUOp[1], Funct_ALU[0]);
  and and_3 (and_3_out, ALUOp[1], Funct_ALU[3]);
  and and_4 (ALU_Control[3], ALUOp[1], Funct_ALU[3], not_1_out);
  or or_1 (ALU_Control[2], ALUOp[0], and_1_out);
  or or_2 (ALU_Control[1], not_2_out, not_3_out);
  or or_3 (ALU_Control[0], and_2_out, and_3_out);

  // Notes on the sheet:
  //   F5
  //   AluOp1
  //   ALUOp0
  //   Don't care
  //   F4
  //   Don't care
  //   F3
  //   F2
  //   F1
  //   F0
  //   ALU Control
  //   Based on fig 4.13 from book
  //   ALU_in_3
  //   ALU_in_2
  //   ALU_in_1
  //   ALU_in_0
endmodule

module ALU (
  input  [31:0] ALUIn_1,
  input  [31:0] ALUIn_2,
  input  [3:0] ALU_ControlBits,
  output ZeroFlag,
  output [31:0] ALU_Out
);

  wire Add_out, comparator_1_lt, Sub_out;
  wire [31:0] adder_1_out, AND_out, bit_extender_1_out, NOR_out, OR_out, subtractor_1_out;

  assign AND_out = ALUIn_1 & ALUIn_2;  // AND_Gate AND, 32 bits wide
  assign OR_out = ALUIn_1 | ALUIn_2;  // OR_Gate OR, 32 bits wide
  Adder #(.width(32)) adder_1 (.a(ALUIn_1), .b(ALUIn_2), .out(adder_1_out), .cout(Add_out));  // open: cin
  Subtractor #(.width(32)) subtractor_1 (
    .a(ALUIn_1), .b(ALUIn_2), .out(subtractor_1_out), .bout(Sub_out));  // open: bin
  Comparator #(.width(32)) comparator_1 (.a(ALUIn_1), .b(ALUIn_2), .lt(comparator_1_lt));  // open: gt, eq
  assign bit_extender_1_out = {{31{1'b0}}, comparator_1_lt};  // Bit_Extender bit_extender_1
  assign NOR_out = ~(ALUIn_1 | ALUIn_2);  // NOR_Gate NOR, 32 bits wide
  Multiplexer #(.select(4), .width(32)) multiplexer_1 (
    .in0(AND_out), .in1(OR_out), .in2(adder_1_out), .in6(subtractor_1_out), .in7(bit_extender_1_out),
    .in12(NOR_out), .out(ALU_Out), .sel(ALU_ControlBits));  // open: in3, in4, in5, in8, in9, in10, in11, in13, in14, in15, en
  Comparator #(.width(32)) comparator_2 (.a({32{1'b0}}), .b(ALU_Out), .eq(ZeroFlag));  // open: gt, lt

  // Notes on the sheet:
  //   ALU - Arithmetic Logic Unit
endmodule

module RegFile (
  input  RegWrite,
  input  [4:0] Read_reg_1,
  input  [4:0] Read_reg_2,
  input  [4:0] WriteReg,
  input  [31:0] WriteData,
  input  Clock,
  output [31:0] Read_data_1,
  output [31:0] Read_data_2
);

  wire demultiplexer_1_out0, demultiplexer_1_out1, demultiplexer_1_out2, demultiplexer_1_out3,
       demultiplexer_1_out4, demultiplexer_1_out5, demultiplexer_1_out6, demultiplexer_1_out7,
       demultiplexer_1_out8, demultiplexer_1_out9, demultiplexer_1_out10, demultiplexer_1_out11,
       demultiplexer_1_out12, demultiplexer_1_out13, demultiplexer_1_out14, demultiplexer_1_out15,
       demultiplexer_1_out16, demultiplexer_1_out17, demultiplexer_1_out18, demultiplexer_1_out19,
       demultiplexer_1_out20, demultiplexer_1_out21, demultiplexer_1_out22, demultiplexer_1_out23,
       demultiplexer_1_out24, demultiplexer_1_out25, demultiplexer_1_out26, demultiplexer_1_out27,
       demultiplexer_1_out28, demultiplexer_1_out29, demultiplexer_1_out30, demultiplexer_1_out31;
  wire [31:0] register_1_q, register_2_q, register_3_q, register_4_q, register_5_q, register_6_q,
       register_7_q, register_8_q, register_9_q, register_10_q, register_11_q, register_12_q, register_13_q,
       register_14_q, register_15_q, register_16_q, register_17_q, register_18_q, register_19_q,
       register_20_q, register_21_q, register_22_q, register_23_q, register_24_q, register_25_q,
       register_26_q, register_27_q, register_28_q, register_29_q, register_30_q, register_31_q,
       register_32_q;

  Demultiplexer #(.select(5)) demultiplexer_1 (
    .out0(demultiplexer_1_out0), .out1(demultiplexer_1_out1), .out2(demultiplexer_1_out2),
    .out3(demultiplexer_1_out3), .out4(demultiplexer_1_out4), .out5(demultiplexer_1_out5),
    .out6(demultiplexer_1_out6), .out7(demultiplexer_1_out7), .out8(demultiplexer_1_out8),
    .out9(demultiplexer_1_out9), .out10(demultiplexer_1_out10), .out11(demultiplexer_1_out11),
    .out12(demultiplexer_1_out12), .out13(demultiplexer_1_out13), .out14(demultiplexer_1_out14),
    .out15(demultiplexer_1_out15), .out16(demultiplexer_1_out16), .out17(demultiplexer_1_out17),
    .out18(demultiplexer_1_out18), .out19(demultiplexer_1_out19), .out20(demultiplexer_1_out20),
    .out21(demultiplexer_1_out21), .out22(demultiplexer_1_out22), .out23(demultiplexer_1_out23),
    .out24(demultiplexer_1_out24), .out25(demultiplexer_1_out25), .out26(demultiplexer_1_out26),
    .out27(demultiplexer_1_out27), .out28(demultiplexer_1_out28), .out29(demultiplexer_1_out29),
    .out30(demultiplexer_1_out30), .out31(demultiplexer_1_out31), .in(RegWrite), .sel(WriteReg));  // open: en
  Register #(.width(32)) register_1 (
    .D(WriteData), .en(demultiplexer_1_out1), .Q(register_1_q), .clk(Clock));  // open: clr
  Register #(.width(32)) register_2 (
    .D(WriteData), .en(demultiplexer_1_out3), .Q(register_2_q), .clk(Clock));  // open: clr
  Register #(.width(32)) register_3 (
    .D(WriteData), .en(demultiplexer_1_out5), .Q(register_3_q), .clk(Clock));  // open: clr
  Register #(.width(32)) register_4 (
    .D(WriteData), .en(demultiplexer_1_out7), .Q(register_4_q), .clk(Clock));  // open: clr
  Register #(.width(32)) register_5 (
    .D(WriteData), .en(demultiplexer_1_out9), .Q(register_5_q), .clk(Clock));  // open: clr
  Register #(.width(32)) register_6 (
    .D(WriteData), .en(demultiplexer_1_out11), .Q(register_6_q), .clk(Clock));  // open: clr
  Register #(.width(32)) register_7 (
    .D(WriteData), .en(demultiplexer_1_out13), .Q(register_7_q), .clk(Clock));  // open: clr
  Register #(.width(32)) register_8 (
    .D(WriteData), .en(demultiplexer_1_out15), .Q(register_8_q), .clk(Clock));  // open: clr
  Register #(.width(32)) register_9 (
    .D(WriteData), .en(demultiplexer_1_out17), .Q(register_9_q), .clk(Clock));  // open: clr
  Register #(.width(32)) register_10 (
    .D(WriteData), .en(demultiplexer_1_out19), .Q(register_10_q), .clk(Clock));  // open: clr
  Register #(.width(32)) register_11 (
    .D(WriteData), .en(demultiplexer_1_out21), .Q(register_11_q), .clk(Clock));  // open: clr
  Register #(.width(32)) register_12 (
    .D(WriteData), .en(demultiplexer_1_out23), .Q(register_12_q), .clk(Clock));  // open: clr
  Register #(.width(32)) register_13 (
    .D(WriteData), .en(demultiplexer_1_out25), .Q(register_13_q), .clk(Clock));  // open: clr
  Register #(.width(32)) register_14 (
    .D(WriteData), .en(demultiplexer_1_out27), .Q(register_14_q), .clk(Clock));  // open: clr
  Register #(.width(32)) register_15 (
    .D(WriteData), .en(demultiplexer_1_out29), .Q(register_15_q), .clk(Clock));  // open: clr
  Register #(.width(32)) register_16 (
    .D(WriteData), .en(demultiplexer_1_out31), .Q(register_16_q), .clk(Clock));  // open: clr
  Register #(.width(32)) register_17 (
    .D(WriteData), .en(demultiplexer_1_out0), .Q(register_17_q), .clk(Clock));  // open: clr
  Register #(.width(32)) register_18 (
    .D(WriteData), .en(demultiplexer_1_out2), .Q(register_18_q), .clk(Clock));  // open: clr
  Register #(.width(32)) register_19 (
    .D(WriteData), .en(demultiplexer_1_out4), .Q(register_19_q), .clk(Clock));  // open: clr
  Register #(.width(32)) register_20 (
    .D(WriteData), .en(demultiplexer_1_out6), .Q(register_20_q), .clk(Clock));  // open: clr
  Register #(.width(32)) register_21 (
    .D(WriteData), .en(demultiplexer_1_out8), .Q(register_21_q), .clk(Clock));  // open: clr
  Register #(.width(32)) register_22 (
    .D(WriteData), .en(demultiplexer_1_out10), .Q(register_22_q), .clk(Clock));  // open: clr
  Register #(.width(32)) register_23 (
    .D(WriteData), .en(demultiplexer_1_out12), .Q(register_23_q), .clk(Clock));  // open: clr
  Register #(.width(32)) register_24 (
    .D(WriteData), .en(demultiplexer_1_out14), .Q(register_24_q), .clk(Clock));  // open: clr
  Register #(.width(32)) register_25 (
    .D(WriteData), .en(demultiplexer_1_out16), .Q(register_25_q), .clk(Clock));  // open: clr
  Register #(.width(32)) register_26 (
    .D(WriteData), .en(demultiplexer_1_out18), .Q(register_26_q), .clk(Clock));  // open: clr
  Register #(.width(32)) register_27 (
    .D(WriteData), .en(demultiplexer_1_out20), .Q(register_27_q), .clk(Clock));  // open: clr
  Register #(.width(32)) register_28 (
    .D(WriteData), .en(demultiplexer_1_out22), .Q(register_28_q), .clk(Clock));  // open: clr
  Register #(.width(32)) register_29 (
    .D(WriteData), .en(demultiplexer_1_out24), .Q(register_29_q), .clk(Clock));  // open: clr
  Register #(.width(32)) register_30 (
    .D(WriteData), .en(demultiplexer_1_out26), .Q(register_30_q), .clk(Clock));  // open: clr
  Register #(.width(32)) register_31 (
    .D(WriteData), .en(demultiplexer_1_out28), .Q(register_31_q), .clk(Clock));  // open: clr
  Register #(.width(32)) register_32 (
    .D(WriteData), .en(demultiplexer_1_out30), .Q(register_32_q), .clk(Clock));  // open: clr
  Multiplexer #(.select(5), .width(32)) multiplexer_1 (
    .in0(register_17_q), .in1(register_1_q), .in2(register_18_q), .in3(register_2_q), .in4(register_19_q),
    .in5(register_3_q), .in6(register_20_q), .in7(register_4_q), .in8(register_21_q), .in9(register_5_q),
    .in10(register_22_q), .in11(register_6_q), .in12(register_23_q), .in13(register_7_q),
    .in14(register_24_q), .in15(register_8_q), .in16(register_25_q), .in17(register_9_q),
    .in18(register_26_q), .in19(register_10_q), .in20(register_27_q), .in21(register_11_q),
    .in22(register_28_q), .in23(register_12_q), .in24(register_29_q), .in25(register_13_q),
    .in26(register_30_q), .in27(register_14_q), .in28(register_31_q), .in29(register_15_q),
    .in30(register_32_q), .in31(register_16_q), .out(Read_data_1), .sel(Read_reg_1));  // open: en
  Multiplexer #(.select(5), .width(32)) multiplexer_2 (
    .in0(register_17_q), .in1(register_1_q), .in2(register_18_q), .in3(register_2_q), .in4(register_19_q),
    .in5(register_3_q), .in6(register_20_q), .in7(register_4_q), .in8(register_21_q), .in9(register_5_q),
    .in10(register_22_q), .in11(register_6_q), .in12(register_23_q), .in13(register_7_q),
    .in14(register_24_q), .in15(register_8_q), .in16(register_25_q), .in17(register_9_q),
    .in18(register_26_q), .in19(register_10_q), .in20(register_27_q), .in21(register_11_q),
    .in22(register_28_q), .in23(register_12_q), .in24(register_29_q), .in25(register_13_q),
    .in26(register_30_q), .in27(register_14_q), .in28(register_31_q), .in29(register_15_q),
    .in30(register_32_q), .in31(register_16_q), .out(Read_data_2), .sel(Read_reg_2));  // open: en

  // Notes on the sheet:
  //   Register File
  //   9
endmodule

module ControlUnit (
  input  [5:0] OPCode,
  output RegDst,
  output AluSrc,
  output MemToReg,
  output RegWrite,
  output Jump,
  output MemRead,
  output MemWrite,
  output Branch,
  output [1:0] ALUOp
);

  wire nor_5_out, nor_6_out, or_1_out;

  nor nor_1 (ALUOp[1], OPCode[0], OPCode[1], OPCode[2], OPCode[3], OPCode[4], OPCode[5]);
  nor nor_2 (ALUOp[0], OPCode[0], OPCode[1], ~OPCode[2], OPCode[3], OPCode[4], OPCode[5]);  // NOR_Gate
  nor nor_3 (MemRead, ~OPCode[0], ~OPCode[1], OPCode[2], OPCode[3], OPCode[4], ~OPCode[5]);  // NOR_Gate
  nor nor_4 (MemWrite, ~OPCode[0], ~OPCode[1], OPCode[2], ~OPCode[3], OPCode[4], ~OPCode[5]);  // NOR_Gate
  nor nor_5 (nor_5_out, OPCode[0], OPCode[1], OPCode[2], ~OPCode[3], OPCode[4], OPCode[5]);  // NOR_Gate
  nor nor_6 (nor_6_out, OPCode[0], ~OPCode[1], OPCode[2], ~OPCode[3], OPCode[4], OPCode[5]);  // NOR_Gate
  nor nor_7 (Jump, OPCode[0], ~OPCode[1], OPCode[2], OPCode[3], OPCode[4], OPCode[5]);  // NOR_Gate
  or or_1 (or_1_out, nor_5_out, nor_6_out);
  or or_2 (RegWrite, ALUOp[1], or_1_out, MemRead);
  or or_3 (AluSrc, MemRead, MemWrite, or_1_out);

  assign Branch = ALUOp[0];
  assign MemToReg = MemRead;
  assign RegDst = ALUOp[1];

  // Notes on the sheet:
  //   Control Unit
endmodule
